// Logisim project CPU.circ as structural Verilog: 2 circuits, main circuit main
module main (
);

  wire alu_1_p2, alu_1_p8, and_1_out, clock, control_1_p3, control_1_p4, registerfile_1_p5,
       registerfile_1_p6, registerfile_1_p7, registerfile_1_p8, registerfile_1_p9, reset;
  wire [2:0] funct, rd, registerfile_1_p3, rs, rt;
  wire [3:0] opcode;
  wire [15:0] adder_1_out, alu_1_p3, alu_1_p6, bit_extender_1_out, inc16_1_p2, multiplexer_2_out,
       multiplexer_3_out, ram_1_dout, register_1_q, registerfile_1_p4;

  // Probe on multiplexer_3_out
  Register #(.width(16)) register_1 (.D(multiplexer_3_out), .clk(clock), .Q(register_1_q), .clr(reset));  // open: en
  ROM #(.addrWidth(16), .dataWidth(16)) rom_1 (.addr(register_1_q), .data({opcode, rs, rt, rd, funct}));
  // Inc16 inc16_1: pin names not known; wires that end beside it: register_1_q, inc16_1_p2
  // Probe on funct
  // Probe on rd
  // Probe on rt
  // Probe on rs
  // Probe on opcode
  // Control control_1: pin names not known; wires that end beside it: opcode, funct, control_1_p3, control_1_p4
  // RegisterFile registerfile_1: pin names not known; wires that end beside it: rs, rt, registerfile_1_p3, registerfile_1_p4, registerfile_1_p5, registerfile_1_p6, registerfile_1_p7, registerfile_1_p8, registerfile_1_p9, clock
  Multiplexer #(.enable("false"), .width(3)) multiplexer_1 (
    .in0(rt), .in1(rd), .out(registerfile_1_p3), .sel(registerfile_1_p8));
  // Probe on registerfile_1_p4
  // Probe on {rd, funct}
  assign bit_extender_1_out = {{10{rd[2]}}, {rd, funct}};  // Bit_Extender bit_extender_1
  // Probe on bit_extender_1_out
  // Probe on registerfile_1_p9
  // Probe on registerfile_1_p7
  Multiplexer #(.enable("false"), .width(16)) multiplexer_2 (
    .in0(alu_1_p3), .in1(bit_extender_1_out), .out(multiplexer_2_out), .sel(registerfile_1_p7));
  // ALU alu_1: pin names not known; wires that end beside it: reset, alu_1_p2, alu_1_p3, alu_1_p2, registerfile_1_p9, alu_1_p6, multiplexer_2_out, alu_1_p8
  Button button_1 (.out(reset));
  Clock clock_1 (.out(clock));
  // Probe on bit_extender_1_out
  Adder #(.width(16)) adder_1 (.a(inc16_1_p2), .b(bit_extender_1_out), .out(adder_1_out));  // open: cin, cout
  and and_1 (and_1_out, control_1_p3, alu_1_p8);
  // Probe on alu_1_p6
  Multiplexer #(.enable("false"), .width(16)) multiplexer_3 (
    .in0(inc16_1_p2), .in1(adder_1_out), .out(multiplexer_3_out), .sel(and_1_out));
  RAM #(.addrWidth(16), .dataWidth(16)) ram_1 (
    .addr(alu_1_p6), .we(registerfile_1_p5), .clk(clock), .din(alu_1_p3), .dout(ram_1_dout));
  Multiplexer #(.enable("false"), .width(16)) multiplexer_4 (
    .in0(alu_1_p6), .in1(ram_1_dout), .out(registerfile_1_p4), .sel(control_1_p4));

  // Notes on the sheet:
  //   PC
  //   contents of rom_1 (hex, n*v repeats v):
  //   5040 508a 3442 5241 303d
endmodule

module milestone2 (
);

  wire alu_1_p8, and_1_out, and_2_out, clock, control_1_p3, control_1_p4, control_1_p6, control_1_p7, j, jal,
       not_1_out, or_1_out, or_2_out, registerfile_1_p6, registerfile_1_p7, registerfile_1_p8,
       registerfile_1_p9, registerfile_1_p10, reset;
  wire [2:0] funct, multiplexer_2_out, rd, registerfile_1_p4, rs, rt;
  wire [3:0] opcode;
  wire [11:0] multiplexer_7_out;
  wire [15:0] adder_1_out, alu_1_p2, alu_1_p3, alu_1_p6, bit_extender_1_out, inc16_1_p2, multiplexer_1_out,
       multiplexer_4_out, multiplexer_5_out, multiplexer_6_out, multiplexer_8_out, ram_1_dout, register_1_q;
  wire [15:12] multiplexer_7_out_2;

  // Probe on multiplexer_5_out
  // Probe on register_1_q
  Register #(.width(16)) register_1 (.D(multiplexer_5_out), .clk(clock), .Q(register_1_q), .clr(reset));  // open: en
  // Inc16 inc16_1: pin names not known; wires that end beside it: register_1_q, inc16_1_p2
  ROM #(.addrWidth(16), .dataWidth(16)) rom_1 (.addr(register_1_q), .data({opcode, rs, rt, rd, funct}));
  // Probe on funct
  // Probe on rd
  // Probe on rt
  // Probe on rs
  // Probe on opcode
  Multiplexer #(.enable("false"), .width(16)) multiplexer_1 (
    .in0(multiplexer_8_out), .in1(inc16_1_p2), .out(multiplexer_1_out), .sel(jal));
  // Control control_1: pin names not known; wires that end beside it: opcode, funct, control_1_p3, control_1_p4, j, control_1_p6, control_1_p7
  Multiplexer #(.enable("false"), .width(3)) multiplexer_2 (
    .in0(rt), .in1(rd), .out(multiplexer_2_out), .sel(registerfile_1_p9));
  // Probe on multiplexer_8_out
  // RegisterFile registerfile_1: pin names not known; wires that end beside it: jal, rs, rt, registerfile_1_p4, multiplexer_1_out, registerfile_1_p6, registerfile_1_p7, registerfile_1_p8, registerfile_1_p9, registerfile_1_p10, clock
  Multiplexer #(.enable("false"), .width(3)) multiplexer_3 (
    .in0(multiplexer_2_out), .in1(3'b111), .out(registerfile_1_p4), .sel(jal));
  // Probe on {rd, funct}
  // Probe on multiplexer_5_out
  assign bit_extender_1_out = {{10{rd[2]}}, {rd, funct}};  // Bit_Extender bit_extender_1
  // Probe on registerfile_1_p8
  // Probe on alu_1_p2
  // Probe on alu_1_p3
  Multiplexer #(.enable("false"), .width(16)) multiplexer_4 (
    .in0(alu_1_p3), .in1(bit_extender_1_out), .out(multiplexer_4_out), .sel(registerfile_1_p8));
  // Probe on bit_extender_1_out
  Multiplexer #(.enable("false"), .width(16)) multiplexer_5 (
    .in0(multiplexer_6_out), .in1(alu_1_p2), .out(multiplexer_5_out), .sel(control_1_p6));
  // Probe on registerfile_1_p10
  // ALU alu_1: pin names not known; wires that end beside it: reset, alu_1_p2, alu_1_p3, alu_1_p2, registerfile_1_p10, alu_1_p6, multiplexer_4_out, alu_1_p8
  Button button_1 (.out(reset));
  Clock clock_1 (.out(clock));
  // Probe on bit_extender_1_out
  Multiplexer #(.enable("false"), .width(16)) multiplexer_6 (
    .in0({multiplexer_7_out_2, multiplexer_7_out}), .in1({multiplexer_7_out_2, rs, rt, rd, funct}),
    .out(multiplexer_6_out), .sel(or_1_out));
  or or_1 (or_1_out, j, jal);
  Adder #(.width(16)) adder_1 (.a(inc16_1_p2), .b(bit_extender_1_out), .out(adder_1_out));  // open: cin, cout
  // Probe on alu_1_p6
  // Probe on {multiplexer_7_out_2, rs, rt, rd, funct}
  not not_1 (not_1_out, alu_1_p8);
  and and_1 (and_1_out, control_1_p3, not_1_out);
  and and_2 (and_2_out, control_1_p4, alu_1_p8);
  RAM #(.addrWidth(16), .dataWidth(16)) ram_1 (
    .addr(alu_1_p6), .we(registerfile_1_p6), .clk(clock), .din(alu_1_p3), .dout(ram_1_dout));
  Multiplexer #(.enable("false"), .width(16)) multiplexer_7 (
    .in0(inc16_1_p2), .in1(adder_1_out), .out({multiplexer_7_out_2, multiplexer_7_out}), .sel(or_2_out));
  or or_2 (or_2_out, and_1_out, and_2_out);
  Multiplexer #(.enable("false"), .width(16)) multiplexer_8 (
    .in0(alu_1_p6), .in1(ram_1_dout), .out(multiplexer_8_out), .sel(control_1_p7));

  // Notes on the sheet:
  //   PC
  //   contents of rom_1 (hex, n*v repeats v):
  //   51a0 d9a 57a8 1040 8006 4026 50c1 667 311b 5dbd 2c40 2dc1 2cc2 527f 8006 1c40 1dc1 1cc2 5d83 5dbd
  //   2cc0 2d01 2d42 2a 41a 222 3103 aea 593f 401a a12 1cc0 1d01 1d42 5d83 7e00 5081 7e00
  //   jr mux
endmodule
